# Fritzing sketch circuit  model1 (saved by Fritzing 0.9.10b)
perfboards: 1

parts:
  R1 = Resistor [tolerance=±5% resistance=220 power=0.25 package=THT]
  J1 = Basic Force Sensing Resistor (FSR) [package=THT]
  L298N1 = L298N DC motor driver
  Power_plug1 = Power plug
  M1 = DC Motor [voltage_(max)=6V voltage_(min)=3V]
  元件1 = Arduino Leonardo (Rev3b)

nets:
  N1: R1.Pin_0, J1.pin_0, 元件1.A0
  GND: R1.Pin_1, L298N1.GND, Power_plug1.GND, 元件1.GND
  N2: J1.pin_1, 元件1.5V
  N3: L298N1.OUT1, M1.pin_2
  N4: L298N1.OUT2, M1.pin_1
  12V: L298N1.12V, Power_plug1.VCC
  N5: L298N1.IN1, 元件1.D6_PWM/A7
  N6: L298N1.IN2, 元件1.D5_PWM

custom parts:
  L298N DC motor driver: 2x DC motor driver with 78M05 positive voltage regulator (7..35 V) L298N: max 46 V, 2 A Set 5 V Enable jumper to enable 5 V regultor (needed for the L298N) and +5 V output at screw terminal or supply external +5 V at screw terminal Set ENA and/or ENB to +5 V to enable motor permanently or supply ENA and/or ENB with PWM signal IN1 and IN2 set rotation directory for motor A (OUT1/OUT2) IN2 and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
