# Fritzing sketch circuit model2 (saved by Fritzing 0.9.10b)
perfboards: 1

parts:
  元件1 = Arduino Uno (Rev3)
  元件2 = RS04
  R1 = Resistor [tolerance=±5% resistance=220 power=0.25 package=THT]
  J1 = Basic Force Sensing Resistor (FSR) [package=THT]
  J16 = Basic Servo
  J17 = Basic Servo
  J18 = Basic Servo
  J19 = Basic Servo
  J20 = Basic Servo
  Power_plug2 = Power plug

nets:
  GND: 元件1.A0, 元件1.GND, 元件2.GND, R1.Pin_1, J16.gnd, J17.gnd, J18.gnd, J19.gnd, J20.gnd, Power_plug2.GND
  N1: 元件1.D8, J19.pulse
  N2: 元件1.D10_PWM/SS, J20.pulse
  N3: 元件1.D12/MISO, 元件2.Echo
  N4: 元件1.D13/SCK, 元件2.Trig
  N5: 元件1.D3_PWM, J16.pulse
  N6: 元件1.D4, J17.pulse
  N7: 元件1.D5_PWM, J18.pulse
  5V: 元件1.5V, 元件2.VCC, J1.pin_1
  N8: R1.Pin_0, J1.pin_0
  VCC: J16.vcc, J17.vcc, J18.vcc, J19.vcc, J20.vcc, Power_plug2.VCC
